# Fritzing sketch Aplikasi Kendali Lampu (saved by Fritzing 0.8.7b)

parts:
  Part1 = Arduino Uno (Rev3)
  U1 = ESP8266 WiFi Module [part_number=ESP8266]
  8_Channel_Relay1 = 8 Channel Power Relay
  LED2 = LEDs [package=led10mm]
  LED3 = LEDs [package=led10mm]
  LED4 = LEDs [package=led10mm]
  LED5 = LEDs [package=led10mm]
  LED6 = LEDs [package=led10mm]
  LED7 = LEDs [package=led10mm]
  LED8 = LEDs [package=led10mm]
  LED9 = LEDs [package=led10mm]
  Part2 = Arduino Uno (Rev3)
  8_Channel_Relay2 = 8 Channel Power Relay
  LED10 = LEDs [package=led10mm]
  LED11 = LEDs [package=led10mm]
  LED12 = LEDs [package=led10mm]
  LED13 = LEDs [package=led10mm]
  LED14 = LEDs [package=led10mm]
  LED15 = LEDs [package=led10mm]
  LED16 = LEDs [package=led10mm]
  LED17 = LEDs [package=led10mm]
  Part3 = Arduino Uno (Rev3)
  U3 = ESP8266 WiFi Module [part_number=ESP8266]
  8_Channel_Relay3 = 8 Channel Power Relay
  LED18 = LEDs [package=led10mm]
  LED19 = LEDs [package=led10mm]
  LED20 = LEDs [package=led10mm]
  LED21 = LEDs [package=led10mm]
  LED22 = LEDs [package=led10mm]
  LED23 = LEDs [package=led10mm]
  LED24 = LEDs [package=led10mm]
  LED25 = LEDs [package=led10mm]

nets:
  N1: Part1.D8, 8_Channel_Relay1.IN7
  N2: Part1.D9_PWM, 8_Channel_Relay1.IN8
  N3: Part1.D12/MISO, U1.RXD
  N4: Part1.D13/SCK, U1.TXD
  GND: Part1.GND, U1.GND, 8_Channel_Relay1.GND
  N5: Part1.D2, 8_Channel_Relay1.IN1
  N6: Part1.D3_PWM, 8_Channel_Relay1.IN2
  N7: Part1.D4, 8_Channel_Relay1.IN3
  N8: Part1.D5_PWM, 8_Channel_Relay1.IN4
  N9: Part1.D6_PWM, 8_Channel_Relay1.IN5
  N10: Part1.D7, 8_Channel_Relay1.IN6
  3V3: Part1.3V3, U1.VCC, U1.GPIO_0, U1.RST, U1.GPIO_2, U1.CH_PD
  5V: Part1.5V, 8_Channel_Relay1.VCC
  N11: 8_Channel_Relay1.COM#22, LED9.A
  N12: 8_Channel_Relay1.NO#23, LED9.C
  N13: 8_Channel_Relay1.COM#25, LED8.A
  N14: 8_Channel_Relay1.NO#26, LED8.C
  N15: 8_Channel_Relay1.COM#28, LED7.A
  N16: 8_Channel_Relay1.NO#29, LED7.C
  N17: 8_Channel_Relay1.COM#31, LED6.A
  N18: 8_Channel_Relay1.NO#32, LED6.C
  N19: 8_Channel_Relay1.COM#34, LED5.A
  N20: 8_Channel_Relay1.NO#35, LED5.C
  N21: 8_Channel_Relay1.COM#37, LED4.A
  N22: 8_Channel_Relay1.NO#38, LED4.C
  N23: 8_Channel_Relay1.COM#40, LED3.A
  N24: 8_Channel_Relay1.NO#41, LED3.C
  N25: 8_Channel_Relay1.COM#43, LED2.A
  N26: 8_Channel_Relay1.NO#44, LED2.C
  N27: Part2.D8, 8_Channel_Relay2.IN7
  N28: Part2.D9_PWM, 8_Channel_Relay2.IN8
  N29: Part2.D2, 8_Channel_Relay2.IN1
  N30: Part2.D3_PWM, 8_Channel_Relay2.IN2
  N31: Part2.D4, 8_Channel_Relay2.IN3
  N32: Part2.D5_PWM, 8_Channel_Relay2.IN4
  N33: Part2.D6_PWM, 8_Channel_Relay2.IN5
  N34: Part2.D7, 8_Channel_Relay2.IN6
  5V_2: Part2.5V, 8_Channel_Relay2.VCC
  GND_2: Part2.GND, 8_Channel_Relay2.GND
  N35: 8_Channel_Relay2.COM#22, LED10.A
  N36: 8_Channel_Relay2.NO#23, LED10.C
  N37: 8_Channel_Relay2.COM#25, LED11.A
  N38: 8_Channel_Relay2.NO#26, LED11.C
  N39: 8_Channel_Relay2.COM#28, LED12.A
  N40: 8_Channel_Relay2.NO#29, LED12.C
  N41: 8_Channel_Relay2.COM#31, LED13.A
  N42: 8_Channel_Relay2.NO#32, LED13.C
  N43: 8_Channel_Relay2.COM#34, LED14.A
  N44: 8_Channel_Relay2.NO#35, LED14.C
  N45: 8_Channel_Relay2.COM#37, LED15.A
  N46: 8_Channel_Relay2.NO#38, LED15.C
  N47: 8_Channel_Relay2.COM#40, LED16.A
  N48: 8_Channel_Relay2.NO#41, LED16.C
  N49: 8_Channel_Relay2.COM#43, LED17.A
  N50: 8_Channel_Relay2.NO#44, LED17.C
  N51: Part3.D12/MISO, U3.RXD
  N52: Part3.D13/SCK, U3.TXD
  GND_3: Part3.GND, U3.GND
  3V3_2: Part3.3V3, U3.VCC, U3.GPIO_2, U3.CH_PD
  N53: 8_Channel_Relay3.COM#22, LED18.A
  N54: 8_Channel_Relay3.NO#23, LED18.C
  N55: 8_Channel_Relay3.COM#25, LED19.A
  N56: 8_Channel_Relay3.NO#26, LED19.C
  N57: 8_Channel_Relay3.COM#28, LED20.A
  N58: 8_Channel_Relay3.NO#29, LED20.C
  N59: 8_Channel_Relay3.COM#31, LED21.A
  N60: 8_Channel_Relay3.NO#32, LED21.C
  N61: 8_Channel_Relay3.COM#34, LED22.A
  N62: 8_Channel_Relay3.NO#35, LED22.C
  N63: 8_Channel_Relay3.COM#37, LED23.A
  N64: 8_Channel_Relay3.NO#38, LED23.C
  N65: 8_Channel_Relay3.COM#40, LED24.A
  N66: 8_Channel_Relay3.NO#41, LED24.C
  N67: 8_Channel_Relay3.COM#43, LED25.A
  N68: 8_Channel_Relay3.NO#44, LED25.C

notes:
  Aplikasi Kendali Lampu Menggunakan Arduino Uno dan ESP8266 Berbasis Android
  Oleh:
  Eka Prawira, S.Kom.
  2014142770
  Univ. Pamulang
  ESP KE ARDUINO BOARD:
  1. TX KE PIN 13
  2. RX KE PIN 12
  3. GND (ESP) KE GND (ARDUINO)
  4. CH/PD DAN VCC (ESP) KE 3V3
  RELAY KE ARDUINO BOARD:
  1. GND (RELAY) KE GND (ARDUINO)
  2. VCC (RELAY) KE 5V
  3. IN 1 KE PIN 2
  4. IN 2 KE PIN 3
  5. IN 3 KE PIN 4
  6. IN 4 KE PIN 5
  7. IN 5 KE PIN 6
  8. IN 6 KE PIN 7
  9. IN 7 KE PIN 8
  10. IN 8 KE PIN 9

custom parts:
  ESP8266 WiFi Module: Generic WiFi Module based on the ESP8266 with onboard PCB antenna and UART communications
  8 Channel Power Relay: An 8 channel power relay. The module operates at 5V.
  LEDs: LEDs Standard schematic elements and footprints for 5mm, 3mm, 1206, and 0603 sized LEDs. 5mm - Spark Fun Electronics SKU : COM-00529 (and others)
